# Fritzing sketch SingleStepper (saved by Fritzing 0.9.3b)
breadboards: 1

parts:
  IC1 = ULN2003A [package="DIP16 [THT]"]
  Microcontroller = Arduino Uno (Rev3) - ICSP
  MOTOR1 = 28BYJ-48 Stepper Motor
  C1 = Capacitor [package=cap-pth-small2]

nets:
  N1: IC1.In_1, Microcontroller.D2
  N2: IC1.In_2, Microcontroller.D3_PWM
  N3: IC1.In_3, Microcontroller.D4
  N4: IC1.In_4, Microcontroller.D5_PWM
  N5: IC1.0V, Microcontroller.GND, C1.2
  N6: IC1.COM_-_Common, Microcontroller.5V, MOTOR1.RED, C1.1
  N7: IC1.Out_4, MOTOR1.ORANGE
  N8: IC1.Out_3, MOTOR1.YELLOW
  N9: IC1.Out_2, MOTOR1.PINK
  N10: IC1.Out_1, MOTOR1.BLUE
